// Logisim project carry_select_adder.circ as structural Verilog: 3 circuits, main circuit main
module main (
  input  [5:0] A,
  input  [5:0] B,
  input  Cin,
  output [5:0] S,
  output Cout
);

  wire C1, C3, C3_0, C3_1, C5_0, C5_1;
  wire [1:0] SG1_0, SG1_1, SG2_0, SG2_1;

  adder2 AD0 (.A(A[1:0]), .B(B[1:0]), .Cin(Cin), .S(S[1:0]), .Cout(C1));
  adder2 AD1_0 (.A(A[3:2]), .B(B[3:2]), .Cin(1'b0), .S(SG1_0), .Cout(C3_0));
  adder2 AD1_1 (.A(A[3:2]), .B(B[3:2]), .Cin(1'b1), .S(SG1_1), .Cout(C3_1));
  adder2 AD2_0 (.A(A[5:4]), .B(B[5:4]), .Cin(1'b0), .S(SG2_0), .Cout(C5_0));
  adder2 AD2_1 (.A(A[5:4]), .B(B[5:4]), .Cin(1'b1), .S(SG2_1), .Cout(C5_1));
  Multiplexer #(.width(2)) multiplexer_1 (.in0(SG1_0), .in1(SG1_1), .out(S[3:2]), .sel(C1));
  Multiplexer multiplexer_2 (.in0(C3_0), .in1(C3_1), .out(C3), .sel(C1));
  Multiplexer #(.width(2)) multiplexer_3 (.in0(SG2_0), .in1(SG2_1), .out(S[5:4]), .sel(C3));
  Multiplexer multiplexer_4 (.in0(C5_0), .in1(C5_1), .out(Cout), .sel(C3));

  // Other names for the same wires on the sheet: CINREAL = Cin; COUTFINAL = Cout; GA0[1:0] = A[1:0];
  //   GA1[1:0] = A[3:2]; GA2[1:0] = A[5:4]; GB0[1:0] = B[1:0]; GB1[1:0] = B[3:2]; GB2[1:0] = B[5:4]; S6OUT[5:0] = S;
  //   SG0[1:0] = S[1:0]; S2_sel = S[2]; S3_sel = S[3]; S4_sel = S[4]; S5_sel = S[5]
endmodule

module full_adder (
  input  A,
  input  B,
  input  Cin,
  output Sum,
  output Cout
);

  wire P1, P2, X1;

  xor xor_1 (X1, A, B);
  and and_1 (P1, A, B);
  xor xor_2 (Sum, X1, Cin);
  and and_2 (P2, X1, Cin);
  or or_1 (Cout, P1, P2);
endmodule

module adder2 (
  input  Cin,
  input  [1:0] A,
  input  [1:0] B,
  output [1:0] S,
  output Cout
);

  wire C1;

  full_adder FA1 (.A(A[1]), .B(B[1]), .Cin(C1), .Sum(S[1]), .Cout(Cout));
  full_adder FA0 (.A(A[0]), .B(B[0]), .Cin(Cin), .Sum(S[0]), .Cout(C1));

  // Other names for the same wires on the sheet: A2[1:0] = A; B2[1:0] = B; COUTF = Cout; S2OUT[1:0] = S
endmodule
